# Fritzing sketch CARRIERELEC (saved by Fritzing 0.8.3b)
circuit board: 5.79431cm x 8.67559cm
breadboards: 1

parts:
  Arduino1 = Arduino
  R1 = Resistor [tolerance=±5% resistance=220 package=THT]
  R2 = Resistor [tolerance=±5% resistance=220 package=THT]
  10k = Resistor [tolerance=±5% resistance=10k package=THT]
  10k_2 = Resistor [tolerance=±5% resistance=10k package=THT]
  C1 = Ceramic Capacitor [capacitance=0.1µF package="100 mil [THT, multilayer]"]
  C2 = Ceramic Capacitor [capacitance=0.1µF package="100 mil [THT, multilayer]"]
  A1_A2_A3_A4_A5 = screw terminal, 5 pins
  RADIO_IN = screw terminal, 5 pins
  13_9_6_5_3 = screw terminal, 5 pins
  5V_GND = screw terminal, 2 pins
  MOTOR = screw terminal, 3 pins
  24V_IN = screw terminal, 2 pins
  RST_GND = screw terminal, 2 pins
  SERIAL = screw terminal, 2 pins
  I2C = screw terminal, 2 pins

nets:
  N1: Arduino1.GND, R2.Pin_1, C1.0, C2.0, 5V_GND.pin2, MOTOR.pin1, 24V_IN.pin2, RST_GND.pin2
  N2: Arduino1.D13, 13_9_6_5_3.pin1
  N3: Arduino1.D12, RADIO_IN.pin1
  N4: Arduino1.D11, 10k.Pin_1
  N5: Arduino1.D10, 10k_2.Pin_1
  N6: Arduino1.D9, 13_9_6_5_3.pin2
  N7: Arduino1.D8, RADIO_IN.pin2
  N8: Arduino1.D7, RADIO_IN.pin3
  N9: Arduino1.D6, 13_9_6_5_3.pin3
  N10: Arduino1.D5, 13_9_6_5_3.pin4
  N11: Arduino1.D4, RADIO_IN.pin4
  N12: Arduino1.D3, 13_9_6_5_3.pin5
  N13: Arduino1.D2, RADIO_IN.pin5
  N14: Arduino1.D1TX, SERIAL.pin1
  N15: Arduino1.D0RX, SERIAL.pin2
  N16: Arduino1.RST, RST_GND.pin1
  N17: Arduino1.VIN, 5V_GND.pin1
  N18: Arduino1.A0, R1.Pin_0, R2.Pin_0
  N19: Arduino1.A1, A1_A2_A3_A4_A5.pin1
  N20: Arduino1.A2, A1_A2_A3_A4_A5.pin2
  N21: Arduino1.A3, A1_A2_A3_A4_A5.pin3
  N22: Arduino1.A4, A1_A2_A3_A4_A5.pin4
  N23: Arduino1.A5, A1_A2_A3_A4_A5.pin5
  N24: Arduino1.SCL, I2C.pin1
  N25: Arduino1.SDA, I2C.pin2
  N26: R1.Pin_1, 24V_IN.pin1
  N27: 10k.Pin_0, C1.1, MOTOR.pin2
  N28: 10k_2.Pin_0, C2.1, MOTOR.pin3

notes:
  SCL SDA
  0v 11 10
  TX RX
  + -
  CARRIER
